// Logisim project COD_Project.circ as structural Verilog: 11 circuits, main circuit Commonbus
module main (
  input  START,
  input  in_2,
  output out_3,
  output out_4,
  output INR,
  output out_6,
  output out_7,
  output out_8,
  output out_9,
  output out_10,
  output out_11,
  output out_12,
  output out_13
);

  wire AC_15, and_1_out, and_2_out, and_3_out, and_4_out, and_5_out, and_6_out, and_7_out, and_8_out,
       and_9_out, and_10_out, and_11_out, and_18_out, and_19_out, and_20_out, and_21_out, and_22_out,
       and_23_out, and_24_out, and_25_out, and_26_out, and_27_out, and_28_out, and_29_out, and_30_out,
       and_32_out, and_36_out, AR_CLR, B0, B1, B2, B3, B4, B5, B6, B7, B8, B9, B10, B11, CLK, D0, D1, D2, D3,
       D4, D5, D6, D7, DR_CLR, I, IR_LD, not_1_out, not_2_out, not_3_out, not_4_out, not_5_out, not_6_out,
       not_7_out, or_1_out, or_6_out, or_15_out, or_16_out, or_17_out, or_18_out, or_19_out, or_24_out,
       or_25_out, r, S0, S1, S2, SS0, SS1, SS2, T0, T2, T3, T4, T5, T6, T7, TR_CLR, TR_INR, TR_LD, WR_EN, X1,
       X2, X3, X4, X5, X7, Y1, Y2, Y3, Y4, Y5;
  wire [14:0] AC_OUT;
  wire [14:12] I_out;
  wire [15:0] commonbus_1_pc_out, DR_OUT;

  Clock clock_1 (.out(CLK));
  not not_1 (not_1_out, out_6);
  and and_1 (and_1_out, INR, not_1_out);
  and and_2 (and_2_out, D1, T5);
  or or_1 (or_1_out, START, and_1_out);
  and and_3 (and_3_out, D0, T5);
  D_Flip_Flop d_ff_1 (.D(or_1_out), .clk(CLK), .Q(INR));  // open: Qn, preset, reset
  or or_2 (S0, X1, X7, X3, X5);
  or or_3 (S1, X3, X7, X2, 1'b0);
  and and_4 (and_4_out, D3, T4);
  or or_4 (S2, X5, X4, 1'b0, X7);
  or or_5 (X4, and_3_out, and_2_out, and_4_out);
  // Probe on commonbus_1_pc_out
  Commonbus commonbus_1 (
    .WR_EN(WR_EN), .OUT_EN(X7), .AR_LD(out_3), .AR_CLR(AR_CLR), .AR_INR(out_4), .SELECTION({S2, S1, S0}),
    .PC_LD(out_12), .PC_CLR(in_2), .PC_INR(out_13), .DR_LD(out_7), .DR_CLR(DR_CLR), .DR_INR(out_8),
    .AC_LD(out_9), .AC_CLR(out_10), .AC_INR(out_11), .IR_LD(IR_LD), .ALU_SELECT({SS2, SS1, SS0}),
    .TR_LD(TR_LD), .TR_CLR(TR_CLR), .TR_INR(TR_INR), .CLK(CLK), .PC_OUT(commonbus_1_pc_out), .DR_OUT(DR_OUT),
    .AC_OUT({AC_15, AC_OUT}), .IR_OUT({I, I_out, B11, B10, B9, B8, B7, B6, B5, B4, B3, B2, B1, B0}));  // open: in_18, ALU_OUT
  and and_5 (and_5_out, D4, T4);
  and and_6 (and_6_out, D5, T5);
  and and_7 (and_7_out, D5, T4);
  and and_8 (and_8_out, D1, T5);
  or or_6 (or_6_out, D0, D1, D2, D6);
  FOURBITCONUTER fourbitconuter_1 (
    .CLK(CLK), .CLR(out_6), .INR(INR), .T0(T0), .T1(IR_LD), .T2(T2), .T3(T3), .T4(T4), .T5(T5), .T6(T6),
    .T7(T7));
  // Probe on {I, I_out, B11, B10, B9, B8, B7, B6, B5, B4, B3, B2, B1, B0}
  and and_9 (and_9_out, D0, T5);
  and and_10 (and_10_out, D2, T5);
  and and_11 (and_11_out, or_6_out, T4);
  // Probe on DR_OUT
  // Probe on {AC_15, AC_OUT}
  or or_7 (X1, and_5_out, and_6_out);
  or or_8 (X2, T0, and_7_out);
  or or_9 (X3, and_9_out, and_8_out, and_10_out);
  or or_10 (X5, T2, 1'b0);
  or or_11 (X7, and_11_out, IR_LD, r);
  Decoder #(.select(3)) decoder_1 (
    .out0(D0), .out1(D1), .out2(D2), .out3(D3), .out4(D4), .out5(D5), .out6(D6), .out7(D7), .sel(I_out));  // open: en
  and and_12 (Y4, B6, r);
  and and_13 (Y5, r, B7);
  and and_14 (Y1, D1, T4);
  and and_15 (Y2, D0, T5);
  and and_16 (Y3, r, B9);
  or or_12 (SS0, Y1, Y3, Y5);
  or or_13 (SS1, Y3, Y2);
  or or_14 (SS2, Y5, Y4);
  not not_2 (not_2_out, I);
  or or_15 (or_15_out, D3, D4);
  not not_3 (not_3_out, I);
  and and_17 (r, D7, not_3_out, T3);
  or or_16 (or_16_out, DR_OUT[0], DR_OUT[1], DR_OUT[2], DR_OUT[3], DR_OUT[4], DR_OUT[5], DR_OUT[6], DR_OUT[7], DR_OUT[8], DR_OUT[9], DR_OUT[10], DR_OUT[11], DR_OUT[12], DR_OUT[13], DR_OUT[14], DR_OUT[15]);
  or or_17 (or_17_out, AC_OUT[0], AC_OUT[1], AC_OUT[2], AC_OUT[3], AC_OUT[4], AC_OUT[5], AC_OUT[6], AC_OUT[7], AC_OUT[8], AC_OUT[9], AC_OUT[10], AC_OUT[11], AC_OUT[12], AC_OUT[13], AC_OUT[14], AC_15);
  and and_18 (and_18_out, T3, not_2_out, D7);
  or or_18 (or_18_out, D0, D1, D2, D5);
  not not_4 (not_4_out, or_16_out);
  not not_5 (not_5_out, AC_15);
  not not_6 (not_6_out, or_17_out);
  and and_19 (and_19_out, D4, T4);
  and and_20 (and_20_out, D5, T5);
  and and_21 (and_21_out, T6, D6, not_4_out);
  and and_22 (and_22_out, r, B4, not_5_out);
  and and_23 (and_23_out, r, B3, AC_15);
  and and_24 (and_24_out, r, B2, not_6_out);
  and and_25 (and_25_out, r, B1);
  and and_26 (and_26_out, T6, D6);
  and and_27 (and_27_out, T5, or_18_out);
  or or_19 (or_19_out, D3, D5);
  and and_28 (and_28_out, T4, or_15_out);
  and and_29 (and_29_out, or_19_out, T4);
  and and_30 (and_30_out, T6, D6);
  or or_20 (out_12, and_19_out, and_20_out);
  or or_21 (out_6, and_27_out, and_26_out, and_28_out, and_18_out);
  or or_22 (out_13, IR_LD, and_21_out, and_22_out, and_23_out, and_24_out, and_25_out);
  or or_23 (WR_EN, and_29_out, and_30_out);
  not not_7 (not_7_out, D7);
  or or_24 (or_24_out, D0, D1, D2);
  and and_31 (out_10, r, B11);
  and and_32 (and_32_out, I, not_7_out, T3);
  or or_25 (or_25_out, D0, D1, D2, D6);
  or or_26 (out_3, T0, T2, and_32_out);
  and and_33 (out_4, D5, T4);
  and and_34 (out_7, or_25_out, T4);
  and and_35 (out_8, D6, T5);
  and and_36 (and_36_out, T5, or_24_out);
  and and_37 (out_11, r, B5);
  or or_27 (out_9, and_36_out, Y1, Y2, Y4, Y5, Y3);

  // Other names for the same wires on the sheet: O0 = I_out[12]; O1 = I_out[13]; O2 = I_out[14]; AC_CLR = out_10;
  //   AC_INR = out_11; AC_LD = out_9; AC_OUT[15] = AC_15; AR_INR = out_4; AR_LD = out_3; DR_INR = out_8;
  //   DR_LD = out_7; I_out (some bits) = {I, B11, B10, B9, B8, B7, B6, B5, B4, B3, B2, B1, B0}; PC_CLR = in_2;
  //   PC_INR = out_13; PC_LD = out_12; SCCLR = out_6; T1 = IR_LD
endmodule

module Commonbus (
  input  WR_EN,
  input  OUT_EN,
  input  AR_LD,
  input  AR_CLR,
  input  AR_INR,
  input  [2:0] SELECTION,
  input  PC_LD,
  input  PC_CLR,
  input  PC_INR,
  input  DR_LD,
  input  DR_CLR,
  input  DR_INR,
  input  AC_LD,
  input  AC_CLR,
  input  AC_INR,
  input  IR_LD,
  input  [2:0] ALU_SELECT,
  input  in_18,
  input  TR_LD,
  input  TR_CLR,
  input  TR_INR,
  input  CLK,
  output [15:0] PC_OUT,
  output [15:0] DR_OUT,
  output [15:0] ALU_OUT,
  output [15:0] AC_OUT,
  output [15:0] IR_OUT
);

  wire [11:0] ar_1_address;
  wire [15:0] adder_1_out, and_1_out, ar_1_dataout, multiplexer_2_out, not_1_out, ram_1_dout, su_1_shl,
       su_1_shr, tr_1_dataout;

  assign not_1_out = ~AC_OUT;  // NOT_Gate not_1, 16 bits wide
  Adder #(.width(16)) adder_1 (.a(DR_OUT), .b(AC_OUT), .out(adder_1_out), .cin(1'b0));  // open: cout
  assign and_1_out = AC_OUT & DR_OUT;  // AND_Gate and_1, 16 bits wide
  SU su_1 (.E(in_18), .SHR(su_1_shr), .SHL(su_1_shl));
  Multiplexer #(.select(3), .width(16)) multiplexer_1 (
    .in1(adder_1_out), .in2(and_1_out), .in3(not_1_out), .in4(su_1_shl), .in5(su_1_shr), .out(ALU_OUT),
    .sel(ALU_SELECT));  // open: in0, in6, in7
  RAM #(.addrWidth(12), .asyncread("true"), .dataWidth(16)) ram_1 (
    .addr(ar_1_address), .we(WR_EN), .oe(OUT_EN), .clk(CLK), .din(multiplexer_2_out), .dout(ram_1_dout));
  AR ar_1 (
    .Load(AR_LD), .CLR(AR_CLR), .CLK(CLK), .INR(AR_INR), .Datain(multiplexer_2_out), .ADDRESS(ar_1_address),
    .Dataout(ar_1_dataout));
  PC pc_1 (.Load(PC_LD), .CLR(PC_CLR), .CLK(CLK), .INR(PC_INR), .Datain(multiplexer_2_out), .Dataout(PC_OUT));
  DR dr_1 (.Load(DR_LD), .Datain(multiplexer_2_out), .CLR(DR_CLR), .CLK(CLK), .INR(DR_INR), .Dataout(DR_OUT));
  AC ac_1 (.Load(AC_LD), .Datain(ALU_OUT), .CLR(AC_CLR), .CLK(CLK), .INR(AC_INR), .Dataout(AC_OUT));
  IR ir_1 (.Load(IR_LD), .Datain(multiplexer_2_out), .CLK(CLK), .Dataout(IR_OUT));
  TR tr_1 (.Load(TR_LD), .Datain(multiplexer_2_out), .CLR(TR_CLR), .CLK(CLK), .INR(TR_INR), .Dataout(tr_1_dataout));
  // Probe on ram_1_dout
  // Probe on tr_1_dataout
  Multiplexer #(.select(3), .width(16)) multiplexer_2 (
    .in1(ar_1_dataout), .in2(PC_OUT), .in3(DR_OUT), .in4(AC_OUT), .in5(IR_OUT), .in6(tr_1_dataout),
    .in7(ram_1_dout), .out(multiplexer_2_out), .sel(SELECTION));  // open: in0
  // Probe on ar_1_address
  // Probe on ar_1_dataout
  // Probe on multiplexer_2_out
  // Probe on IR_OUT
  // Probe on PC_OUT
endmodule

module AC (
  input  Load,
  input  [15:0] Datain,
  input  CLR,
  input  CLK,
  input  INR,
  output [15:0] Dataout
);

  wire [15:0] adder_1_out, multiplexer_1_out, multiplexer_2_out, multiplexer_3_out;

  Adder #(.width(16)) adder_1 (.a(16'h1), .b(Dataout), .out(adder_1_out), .cin(1'b0));  // open: cout
  Multiplexer #(.enable("true"), .width(16)) multiplexer_1 (
    .in0(Dataout), .in1(adder_1_out), .out(multiplexer_1_out), .sel(INR));  // open: en
  Multiplexer #(.enable("true"), .width(16)) multiplexer_2 (
    .in0(multiplexer_1_out), .in1({16{1'b0}}), .out(multiplexer_2_out), .sel(CLR));  // open: en
  Multiplexer #(.enable("true"), .width(16)) multiplexer_3 (
    .in0(multiplexer_2_out), .in1(Datain), .out(multiplexer_3_out), .sel(Load));  // open: en
  Register #(.width(16)) register_1 (.D(multiplexer_3_out), .clk(CLK), .Q(Dataout));  // open: en, clr

  // Other names for the same wires on the sheet: Input[15:0] = Datain; LD = Load; Output[15:0] = Dataout
endmodule

module DR (
  input  Load,
  input  [15:0] Datain,
  input  CLR,
  input  CLK,
  input  INR,
  output [15:0] Dataout
);

  wire [15:0] adder_1_out, multiplexer_1_out, multiplexer_2_out, multiplexer_3_out;

  Adder #(.width(16)) adder_1 (.a(16'h1), .b(Dataout), .out(adder_1_out), .cin(1'b0));  // open: cout
  Multiplexer #(.enable("true"), .width(16)) multiplexer_1 (
    .in0(Dataout), .in1(adder_1_out), .out(multiplexer_1_out), .sel(INR));  // open: en
  Multiplexer #(.enable("true"), .width(16)) multiplexer_2 (
    .in0(multiplexer_1_out), .in1({16{1'b0}}), .out(multiplexer_2_out), .sel(CLR));  // open: en
  Multiplexer #(.enable("true"), .width(16)) multiplexer_3 (
    .in0(multiplexer_2_out), .in1(Datain), .out(multiplexer_3_out), .sel(Load));  // open: en
  Register #(.width(16)) register_1 (.D(multiplexer_3_out), .clk(CLK), .Q(Dataout));  // open: en, clr

  // Other names for the same wires on the sheet: Input[15:0] = Datain; LD = Load; Output[15:0] = Dataout
endmodule

module IR (
  input  Load,
  input  [15:0] Datain,
  input  CLK,
  output [15:0] Dataout
);

  wire [15:0] multiplexer_1_out;

  Multiplexer #(.enable("true"), .width(16)) multiplexer_1 (
    .in0(Dataout), .in1(Datain), .out(multiplexer_1_out), .sel(Load));  // open: en
  // Probe on Dataout
  Register #(.width(16)) register_1 (.D(multiplexer_1_out), .clk(CLK), .Q(Dataout));  // open: en, clr

  // Other names for the same wires on the sheet: DATA_IN[15:0] = Datain; DATA_OUT[15:0] = Dataout; LD = Load
endmodule

module TR (
  input  Load,
  input  [15:0] Datain,
  input  CLR,
  input  CLK,
  input  INR,
  output [15:0] Dataout
);

  wire [15:0] adder_1_out, multiplexer_1_out, multiplexer_2_out, multiplexer_3_out;

  Adder #(.width(16)) adder_1 (.a(16'h1), .b(Dataout), .out(adder_1_out), .cin(1'b0));  // open: cout
  Multiplexer #(.enable("true"), .width(16)) multiplexer_1 (
    .in0(Dataout), .in1(adder_1_out), .out(multiplexer_1_out), .sel(INR));  // open: en
  Multiplexer #(.enable("true"), .width(16)) multiplexer_2 (
    .in0(multiplexer_1_out), .in1({16{1'b0}}), .out(multiplexer_2_out), .sel(CLR));  // open: en
  Multiplexer #(.enable("true"), .width(16)) multiplexer_3 (
    .in0(multiplexer_2_out), .in1(Datain), .out(multiplexer_3_out), .sel(Load));  // open: en
  Register #(.width(16)) register_1 (.D(multiplexer_3_out), .clk(CLK), .Q(Dataout));  // open: en, clr

  // Other names for the same wires on the sheet: Input[15:0] = Datain; LD = Load; Output[15:0] = Dataout
endmodule

module PC (
  input  Load,
  input  CLR,
  input  CLK,
  input  INR,
  input  [15:0] Datain,
  output [15:0] Dataout
);

  wire [11:0] adder_1_out, multiplexer_1_out, multiplexer_2_out, multiplexer_3_out;

  Adder #(.width(12)) adder_1 (.a(12'h1), .b(Dataout[11:0]), .out(adder_1_out));  // open: cin, cout
  Multiplexer #(.enable("true"), .width(12)) multiplexer_1 (
    .in0(Dataout[11:0]), .in1(adder_1_out), .out(multiplexer_1_out), .sel(INR));  // open: en
  Multiplexer #(.enable("true"), .width(12)) multiplexer_2 (
    .in0(multiplexer_1_out), .in1({12{1'b0}}), .out(multiplexer_2_out), .sel(CLR));  // open: en
  Multiplexer #(.enable("true"), .width(12)) multiplexer_3 (
    .in0(multiplexer_2_out), .in1(Datain[11:0]), .out(multiplexer_3_out), .sel(Load));  // open: en
  Register #(.width(12)) register_1 (.D(multiplexer_3_out), .clk(CLK), .Q(Dataout[11:0]));  // open: en, clr

  assign Dataout[15:12] = 4'b0000;

  // Other names for the same wires on the sheet: Input[11:0] = Datain[11:0]; Output[11:0] = Dataout[11:0]; LD = Load
endmodule

module AR (
  input  Load,
  input  CLR,
  input  CLK,
  input  INR,
  input  [15:0] Datain,
  output [11:0] ADDRESS,
  output [15:0] Dataout
);

  wire [11:0] adder_1_out, multiplexer_1_out, multiplexer_2_out, multiplexer_3_out;

  Adder #(.width(12)) adder_1 (.a(ADDRESS), .b(12'h1), .out(adder_1_out));  // open: cin, cout
  Multiplexer #(.enable("true"), .width(12)) multiplexer_1 (
    .in0(ADDRESS), .in1(adder_1_out), .out(multiplexer_1_out), .sel(INR));  // open: en
  Multiplexer #(.enable("true"), .width(12)) multiplexer_2 (
    .in0(multiplexer_1_out), .in1({12{1'b0}}), .out(multiplexer_2_out), .sel(CLR));  // open: en
  Multiplexer #(.enable("true"), .width(12)) multiplexer_3 (
    .in0(multiplexer_2_out), .in1(Datain[11:0]), .out(multiplexer_3_out), .sel(Load));  // open: en
  Register #(.width(12)) register_1 (.D(multiplexer_3_out), .clk(CLK), .Q(ADDRESS));  // open: en, clr

  assign Dataout = {4'b0000, ADDRESS};

  // Other names for the same wires on the sheet: LD = Load
endmodule

module FOURBITCONUTER (
  input  CLK,
  input  CLR,
  input  INR,
  output T0,
  output T1,
  output T2,
  output T3,
  output T4,
  output T5,
  output T6,
  output T7
);

  wire undriven;
  wire [2:0] adder_1_out, multiplexer_1_out, multiplexer_2_out, Output;

  Adder #(.width(3)) adder_1 (.a(3'b001), .b(Output), .out(adder_1_out), .cin(undriven));  // open: cout
  Multiplexer #(.enable("true"), .width(3)) multiplexer_1 (
    .in0(Output), .in1(adder_1_out), .out(multiplexer_1_out), .sel(INR));  // open: en
  Multiplexer #(.enable("true"), .width(3)) multiplexer_2 (
    .in0(multiplexer_1_out), .in1(3'b000), .out(multiplexer_2_out), .sel(CLR));  // open: en
  Decoder #(.select(3)) decoder_1 (
    .out0(T0), .out1(T1), .out2(T2), .out3(T3), .out4(T4), .out5(T5), .out6(T6), .out7(T7), .sel(Output));  // open: en
  Register #(.width(3)) register_1 (.D(multiplexer_2_out), .clk(CLK), .Q(Output));  // open: en, clr
endmodule

module SU (
  input  E,
  output [15:0] SHR,
  output [15:0] SHL
);

  AC ac_1 (.Dataout({E, SHL[15:2], E}));  // open: Load, Datain, CLR, CLK, INR

  assign SHL[1:0] = {2{E}};
  assign SHR = {{2{E}}, SHL[15:2]};
endmodule

module EREGISTER (
  input  COM_E,
  input  CLR,
  input  [15:0] COUTLOAD,
  input  LD,
  input  CLK
);

  wire [15:0] E_FF, multiplexer_1_out, multiplexer_2_out, multiplexer_3_out, not_1_out;

  assign not_1_out = ~E_FF;  // NOT_Gate not_1, 16 bits wide
  Multiplexer #(.enable("true"), .width(16)) multiplexer_1 (
    .in0(E_FF), .in1(not_1_out), .out(multiplexer_1_out), .sel(COM_E));  // open: en
  Multiplexer #(.enable("true"), .width(16)) multiplexer_2 (
    .in0(multiplexer_1_out), .in1({16{1'b0}}), .out(multiplexer_2_out), .sel(CLR));  // open: en
  Multiplexer #(.enable("true"), .width(16)) multiplexer_3 (
    .in0(multiplexer_2_out), .in1(COUTLOAD), .out(multiplexer_3_out), .sel(LD));  // open: en
  Register #(.width(16)) register_1 (.D(multiplexer_3_out), .clk(CLK), .Q(E_FF));  // open: en, clr
endmodule
